# Fritzing sketch AutoCAR (saved by Fritzing 0.9.3b)

parts:
  LEFT = hc-sr04
  BACK = hc-sr04
  FRONT = hc-sr04
  RIGHT = hc-sr04
  Součástka2 = Arduino Mega 2560 (Rev3)

nets:
  VCC: LEFT.VCC, BACK.VCC, FRONT.VCC, RIGHT.VCC, Součástka2.5V
  N1: LEFT.Trig, Součástka2.D53
  N2: LEFT.Echo, Součástka2.D52
  GND: LEFT.GND, BACK.GND, FRONT.GND, RIGHT.GND, Součástka2.GND
  N3: BACK.Trig, Součástka2.D51
  N4: BACK.Echo, Součástka2.D50
  N5: FRONT.Trig, Součástka2.D49
  N6: FRONT.Echo, Součástka2.D48
  N7: RIGHT.Trig, Součástka2.D23
  N8: RIGHT.Echo, Součástka2.D22
